// Digital circuit solucao.dig as structural Verilog
module solucao (
  input  INTD,
  input  INTC,
  input  INTB,
  input  INTA,
  input  M,
  input  SA,
  input  SB,
  input  SC,
  input  SD,
  output Y
);

  wire multiplexer_2_out;
  wire [1:0] priorityencoder_1_num;

  Multiplexer multiplexer_1 (.sel(M), .in_0(INTA), .in_1(multiplexer_2_out), .out(Y));
  PriorityEncoder #(.Selector_Bits(2)) priorityencoder_1 (
    .in0(SA), .in1(SB), .in2(SC), .in3(SD), .num(priorityencoder_1_num));  // open: any
  Multiplexer #(.Selector_Bits(2)) multiplexer_2 (
    .sel(priorityencoder_1_num), .in_0(INTA), .in_1(INTB), .in_2(INTC), .in_3(INTD), .out(multiplexer_2_out));
endmodule
